# Fritzing sketch parking final (saved by Fritzing 0.9.3b)
breadboards: 2

parts:
  Tastatura2 = Tastatura  # not connected
  FRDM2 = Freescale FRDM KL25Z  # not connected
  Banggood_Display2 = Banggood Display
  U2 = NodeMCU V1.0  # not connected
  FRDM3 = Freescale FRDM KL25Z  # not connected
  J1 = Infrared Proximity Sensor  # not connected

nets:
  N1: Banggood_Display2.VCC, Banggood_Display2.LED

custom parts:
  Freescale FRDM KL25Z: Freescale FRDM razvojni sistem
  NodeMCU V1.0: ESP8266 based NodeMCU
